# Fritzing sketch stackduino-2-smd (saved by Fritzing 0.8.3b)
breadboards: 6

parts:
  Power_plug2 = Power plug
  Btn_3 = Pushbutton 12mm omron
  Encoder1 = Rotary Encoder with Knob
  Btn_4 = Pushbutton [package="[THT]"]
  Btn_5 = Pushbutton [package="[THT]"]
  C7 = Ceramic Capacitor [capacitance=0.1µF package="0805 [SMD, multilayer]"]  # not connected
  X1 = USB Connectors [package=usb-microb]
  C8 = Ceramic Capacitor [capacitance=100nF package="0805 [SMD, multilayer]"]  # not connected
  C9 = Ceramic Capacitor [capacitance=100nF package="0805 [SMD, multilayer]"]  # not connected
  C10 = Ceramic Capacitor [capacitance=100nF package="0805 [SMD, multilayer]"]
  C11 = Ceramic Capacitor [capacitance=100nF package="0805 [SMD, multilayer]"]
  R2 = Resistor [tolerance=±5% resistance=220 package="1206 [SMD]"]  # not connected
  U2 = ATmega328 [package=tqfp]
  R3 = Resistor [tolerance=±5% resistance=220 package="1206 [SMD]"]  # not connected
  R1 = Resistor [tolerance=±5% resistance=220 package="1206 [SMD]"]  # not connected
  XTAL1 = Crystal [frequency="16 Mhz" package=SMD]
  IC1 = USB to UART Bridge - FT232RL [chip_label=IC package=SSOP28DB]
  L1 = Inductors [package=cdrh2d09]
  LTC1 = LTC4412 [package=ThinSOT]
  IC2 = ILD213T [package=so08]  # not connected
  MC34063A1 = MC34063A [package=so08]
  DB1 = DB15_rt_female
  A1 = Allegro A3967 [part_number=" A3967" chip_label=" A3967" package=SOIC-24]
  J1 = Dig-ole 128 x 64 0.96" OLED Display [form="♀ (female)" package=THT]  # not connected
  Power_plug3 = Power plug
  R4 = Resistor [tolerance=±5% resistance=220 package=THT]
  C12 = Electrolytic Capacitor [capacitance=1µF package="100 mil [THT, electrolytic]"]
  C13 = Electrolytic Capacitor [capacitance=1µF package="100 mil [THT, electrolytic]"]
  R5 = Resistor [tolerance=±5% resistance=220 package=THT]
  D1 = Rectifier Diode [part_number=1N4001 package="300 mil [THT]"]
  C14 = Ceramic Capacitor [capacitance=100nF package="100 mil [THT, multilayer]"]
  D2 = Rectifier Diode [part_number=1N4001 package="300 mil [THT]"]
  Q1 = PNP-Transistor [package="TO92 [THT]"]
  R6 = Resistor [tolerance=±5% resistance=220 package=THT]
  C15 = Ceramic Capacitor [capacitance=100nF package="100 mil [THT, multilayer]"]
  C16 = Ceramic Capacitor [capacitance=100nF package="100 mil [THT, multilayer]"]
  C17 = Ceramic Capacitor [capacitance=100nF package="100 mil [THT, multilayer]"]
  C18 = Ceramic Capacitor [capacitance=100nF package="100 mil [THT, multilayer]"]
  C19 = Ceramic Capacitor [capacitance=100nF package="100 mil [THT, multilayer]"]
  C20 = Ceramic Capacitor [capacitance=100nF package="100 mil [THT, multilayer]"]
  R7 = Resistor [tolerance=±5% resistance=220 package=THT]
  C21 = Ceramic Capacitor [capacitance=100nF package="100 mil [THT, multilayer]"]
  J2 = double row female pin header, 6 pins [form="♀ (female)"]
  C22 = Electrolytic Capacitor [capacitance=1µF package="100 mil [THT, electrolytic]"]
  R8 = Trimmer Potentiometer [maximum_resistance=10kΩ package=THT]
  R9 = Resistor [tolerance=±5% resistance=220 package=THT]
  R10 = Resistor [tolerance=±5% resistance=220 package=THT]
  R11 = Resistor [tolerance=±5% resistance=220 package=THT]
  R12 = Resistor [tolerance=±5% resistance=220 package=THT]
  R13 = Resistor [tolerance=±5% resistance=220 package=THT]
  R14 = Resistor [tolerance=±5% resistance=220 package=THT]
  C23 = Ceramic Capacitor [capacitance=100nF package="100 mil [THT, multilayer]"]
  R15 = Resistor [tolerance=±5% resistance=220 package=THT]
  C24 = Ceramic Capacitor [capacitance=100nF package="100 mil [THT, multilayer]"]
  MCP2 = MCP23017 Port Expander [chip_label=IC package=SSOP28DB]
  R16 = Resistor [tolerance=±5% resistance=220 package=THT]
  R17 = Resistor [tolerance=±5% resistance=220 package=THT]

nets:
  N1: Power_plug2.VCC, D2.anode
  GND: Btn_3.Pin_4, Encoder1.no_name_yet#2, Encoder1.no_name_yet#5, Btn_4.Pin_3, Btn_4.Pin_4, Btn_5.Pin_3, Btn_5.Pin_4, X1.GND, C10.1, C11.0, U2.GND, U2.AGND, IC1.7, IC1.18, IC1.21, IC1.25, LTC1.2, LTC1.3, MC34063A1.4, DB1.1, DB1.6, DB1.11, A1.Pin_6, A1.Pin_7, A1.Pin_18, A1.Pin_19, C12.-, C13.-, R5.Pin_1, D1.cathode, C14.0, C15.0, C16.0, C17.0, C18.0, C19.0, C20.0, J2.pin6, R9.Pin_1, R10.Pin_0, R12.Pin_0, R14.Pin_0, C23.0, R15.Pin_1, C24.0, MCP2.10
  N2: Btn_4.Pin_1, Btn_4.Pin_2
  N3: Btn_5.Pin_1, Btn_5.Pin_2
  N4: X1.D+, IC1.15
  N5: X1.D-, IC1.16
  N6: X1.VBUS, IC1.4, IC1.20, C17.1, C19.1, C20.1
  N7: C10.0, U2.PB7(XTAL2_TOSC2), XTAL1.pin_1
  N8: C11.1, U2.PB6(XTAL1_TOSC1), XTAL1.pin_0
  N9: U2.VCC, U2.AVCC, U2.AREF, L1.2, MC34063A1.5, A1.Pin_14, C13.+, R5.Pin_0, R6.Pin_1, C15.1, C16.1, R7.Pin_0, J2.pin2, R8.leg2, R11.Pin_1, R13.Pin_0, MCP2.9
  N10: U2.PB3(MOSI_OC2), J2.pin4
  N11: U2.PB4(MISO), J2.pin1
  N12: U2.PB5(SCK), J2.pin3
  N13: U2.PC4(ADC4_SDA), MCP2.13, R17.Pin_1
  N14: U2.PC5(ADC5_SCL), MCP2.12, R16.Pin_1
  N15: U2.PC6(_RESET), R7.Pin_1, C21.0, J2.pin5
  N16: U2.PD0(RXD), IC1.5
  N17: U2.PD1(TXD), IC1.1
  N18: U2.PD2(INT0), MCP2.19
  N19: IC1.2, C21.1
  N20: IC1.17, C18.1
  N21: L1.1, MC34063A1.2, D1.anode
  N22: LTC1.1, Power_plug3.GND
  N23: LTC1.4, R6.Pin_0
  N24: LTC1.5, Q1.B
  N25: LTC1.6, MC34063A1.6, A1.Pin_5, A1.Pin_20, R4.Pin_1, C12.+, D2.cathode, C22.+
  N26: MC34063A1.1, MC34063A1.7, MC34063A1.8, R4.Pin_0
  N27: MC34063A1.3, C14.1
  N28: DB1.12, A1.Pin_16
  N29: DB1.13, A1.Pin_21
  N30: DB1.14, A1.Pin_9
  N31: DB1.15, A1.Pin_4
  N32: A1.Pin_1, R8.wiper
  N33: A1.Pin_2, R15.Pin_0, C24.1
  N34: A1.Pin_8, R11.Pin_0
  N35: A1.Pin_15, R12.Pin_1
  N36: A1.Pin_17, R10.Pin_1
  N37: A1.Pin_22, R13.Pin_1
  N38: A1.Pin_23, R14.Pin_1, C23.1
  N39: Power_plug3.VCC, Q1.E
  N40: R8.leg1, R9.Pin_0
  N41: MCP2.18, R16.Pin_0, R17.Pin_0

notes:
  ATMEGA
  Regulated 5v
  Unregulated Vin
  DC Adapter
  Battery
  POWER
  A3967
  FT232RL
  ICSP
  MCP23017
  DB15

custom parts:
  Pushbutton 12mm omron: A generic pushbutton. 12mm
  Rotary Encoder with Knob: Rotary Encoder with 1/4" Shaft and Knob
  LTC4412: Low Loss Powerpath Controller
  MC34063A: 1.5 A, Step-Up/Down/Inverting Switching Regulator
  DB15_rt_female: 15 pin, right-angle female VGA connector. Based on DB9 part by Don Roberts.
  Allegro A3967: Allegro A3967 stepper motor driver in SOIC 24 package
